// Logisim project pipeline_2.circ as structural Verilog: 18 circuits, main circuit main
module main (
  input  rst,
  output Cr
);

  wire ALUsell, bensig, Beq, Bne, CLK, controlnew_1_memread, controlnew_1_memtoreg, controlnew_1_memwrite,
       controlnew_1_regwrite, ex_1_aluopo, ex_1_memreado, ex_1_memreg, ex_1_memwriteo, ExReg_write, J, j2,
       M3S, mem_1_memreado, mem_1_memreg, mem_1_memwriteo, MeMReg_write, PcSrc, RegDst, undriven,
       WBReg_write, Zr;
  wire [1:0] controlsigs_1_alu, fowrA, fowrB, register_2_q, SALUtunel;
  wire [4:0] iftoid_rdo, multiplexer_2_out, RaAtunnel, RbAtunel, Rd2, Rd3, Rd4, RDtans, RStans, RTtans;
  wire [5:0] OPCODE;
  wire [15:0] iftoid_imm16, value;
  wire [23:0] adder_1_out, controlsigs_1_addres, iftoid_opc, J_BR_Addres, multiplexer_1_out, pc;
  wire [25:0] imm26;
  wire [31:0] A, ALU_1_z, Ao, B, Bo, extomem_alu_out, idtoex_a_out, idtoex_b_out, insttrans,
       multiplexer_5_out, multiplexer_6_out, RzDtunel;
  wire [60:0] controlunit_1_inst;

  Multiplexer #(.width(24)) multiplexer_1 (.in0(adder_1_out), .in1(J_BR_Addres), .out(multiplexer_1_out), .sel(PcSrc));
  pctoif u_pc (.enable(1'b1), .clk(CLK), .reset(rst), .pc_iput(multiplexer_1_out), .out_5(pc));
  Adder #(.width(24)) adder_1 (.a(24'h1), .b(pc), .out(adder_1_out));  // open: cin, cout
  ROM #(.addrWidth(24), .dataWidth(32)) RegisterMemory (.addr(pc), .data(insttrans));
  ControlUnit controlunit_1 (.mips(insttrans), .counter(pc), .Inst(controlunit_1_inst));
  Register #(.width(1)) register_1 (.D(undriven), .en(1'b1), .clk(CLK), .clr(rst));  // open: Q
  controlSigs controlsigs_1 (
    .translated_in(controlunit_1_inst), .bne(bensig), .addres(controlsigs_1_addres), .dz(RDtans),
    .ma(RStans), .jump(J), .m3sel(ALUsell), .alu(controlsigs_1_alu), .mb(RTtans));  // open: value, en
  if_id iftoid (
    .inPC(pc), .clk(CLK), .rt(RTtans), .rd(RDtans), .rs(RStans), .reset(rst), .INST(insttrans),
    .OPC(iftoid_opc), .rto(RbAtunel), .rdo(iftoid_rdo), .rso(RaAtunnel), .IMM16(iftoid_imm16), .IMM26(imm26),
    .op(OPCODE));
  Clock clock_1 (.out(CLK));
  Register #(.width(2)) register_2 (.D(controlsigs_1_alu), .en(1'b1), .clk(CLK), .Q(register_2_q), .clr(rst));
  CONTROLNEW controlnew_1 (
    .Opcode(OPCODE), .bne(Bne), .MemRead(controlnew_1_memread), .MemWrite(controlnew_1_memwrite),
    .RegDst(RegDst), .RegWrite(controlnew_1_regwrite), .MemtoReg(controlnew_1_memtoreg));
  next_pc next_pc_1 (
    .INCpc(iftoid_opc), .J(j2), .ADDRES_J(imm26), .bNE(Bne), .Ainput(Ao), .Binput(Bo), .PCSrc(PcSrc),
    .J_OR_BR_ADDRES(J_BR_Addres));
  REGISTER0to7 fileRegister (
    .RzD(RzDtunel), .RST(rst), .CLK(CLK), .RaA(RaAtunnel), .RbA(RbAtunel), .RzA(Rd4), .EnableReEn(Rd4),
    .RaD(A), .RbD(B));
  Multiplexer #(.width(5)) multiplexer_2 (.in0(RbAtunel), .in1(iftoid_rdo), .out(multiplexer_2_out), .sel(RegDst));
  Register #(.width(2)) register_3 (.D(register_2_q), .en(1'b1), .clk(CLK), .Q(SALUtunel), .clr(rst));
  Multiplexer #(.select(2), .width(32)) multiplexer_3 (
    .in0(A), .in1(ALU_1_z), .in2(multiplexer_6_out), .in3(RzDtunel), .out(Ao), .sel(fowrA));
  Multiplexer #(.select(2), .width(32)) multiplexer_4 (
    .in0(B), .in1(ALU_1_z), .in2(multiplexer_6_out), .in3(RzDtunel), .out(Bo), .sel(fowrB));
  EX ex_1 (
    .ALUop(ALUsell), .BNE(bensig), .ALUSrc(J), .MemRead(controlnew_1_memread),
    .MemWrite(controlnew_1_memwrite), .MemtoReg(controlnew_1_memtoreg), .RegWrite(controlnew_1_regwrite),
    .RST(rst), .CLK(CLK), .BNEout(Bne), .BEQout(Beq), .MemReadO(ex_1_memreado), .MemWriteO(ex_1_memwriteo),
    .RegwriteO(ExReg_write), .MemReg(ex_1_memreg), .AluSrcO(j2), .ALuopO(ex_1_aluopo));  // open: BEQ, J, Jout
  id_ex idtoex (
    .clk(CLK), .reset(rst), .Rd2in(multiplexer_2_out), .A_input(Ao), .B_input(Bo), .imm16(iftoid_imm16),
    .im16(value), .Rd2(Rd2), .A_out(idtoex_a_out), .B_out(idtoex_b_out));  // open: J_add, Pc, func, fun, J_addrs, Npc
  Multiplexer #(.width(32)) multiplexer_5 (
    .in0(idtoex_b_out), .in1({{16{1'b0}}, value}), .out(multiplexer_5_out), .sel(M3S));
  Hazard hazard_1 (
    .Rt(RbAtunel), .Rs(RaAtunnel), .EX_Regwrite(ExReg_write), .Rd2(Rd2), .MEM_Regwrite(MeMReg_write),
    .Rd3(Rd3), .WB_Regwrite(WBReg_write), .Rd4(Rd4), .ForwardA(fowrA), .ForwardB(fowrB));
  AlU ALU_1 (.a(idtoex_a_out), .b(multiplexer_5_out), .S1S0(SALUtunel), .Z(ALU_1_z), .Cr(Cr), .Zr(Zr));
  Register #(.width(1)) register_4 (.D(ex_1_aluopo), .en(1'b1), .clk(CLK), .Q(M3S), .clr(rst));
  ex_mem extomem (.clk(CLK), .reset(rst), .alu_input(ALU_1_z), .Rd3in(Rd2), .alu_out(extomem_alu_out), .Rd3(Rd3));
  MEM mem_1 (
    .MemRead(ex_1_memreado), .MemWrite(ex_1_memwriteo), .MemtoReg(ex_1_memreg), .RegWrite(ExReg_write),
    .RST(rst), .CLK(CLK), .MemReadO(mem_1_memreado), .MemWriteO(mem_1_memwriteo), .RegwriteO(MeMReg_write),
    .MemReg(mem_1_memreg));
  RAM #(.addrWidth(24), .dataWidth(32)) theram (
    .addr(extomem_alu_out[23:0]), .we(mem_1_memreado), .oe(mem_1_memwriteo));  // open: clk, din, dout
  Multiplexer #(.width(32)) multiplexer_6 (
    .in0(extomem_alu_out), .out(multiplexer_6_out), .sel(mem_1_memreg));  // open: in1
  mem_wb memtowb (.clk(CLK), .reset(rst), .mem_in(multiplexer_6_out), .Rd4in(Rd3), .Rd4(Rd4), .mem_out(RzDtunel));
  WB wb_1 (.reg_write_in(MeMReg_write), .clk(CLK), .rest(rst), .reg_write(WBReg_write));
  // also tied to GND on the sheet: {extomem_alu_out[24], extomem_alu_out[25], extomem_alu_out[26], extomem_alu_out[27], extomem_alu_out[28], extomem_alu_out[29], extomem_alu_out[30], extomem_alu_out[31]}

  // Notes on the sheet:
  //   contents of RegisterMemory (hex, n*v repeats v):
  //   0 2230000a 2272000f 250a020 1651fffc
endmodule

module AlU (
  input  [31:0] a,
  input  [31:0] b,
  input  [1:0] S1S0,
  output Cr,
  output [31:0] Z,
  output Zr
);

  wire adder_1_cout, nor_1_out, nor_2_out, subtractor_1_bout;
  wire [31:0] adder_1_out, and_1_out, or_1_out, subtractor_1_out;

  nor nor_1 (nor_1_out, subtractor_1_out[0], subtractor_1_out[1], subtractor_1_out[2], subtractor_1_out[3], subtractor_1_out[4], subtractor_1_out[5], subtractor_1_out[6], subtractor_1_out[7], subtractor_1_out[8], subtractor_1_out[9], subtractor_1_out[10], subtractor_1_out[11], subtractor_1_out[12], subtractor_1_out[13], subtractor_1_out[14], subtractor_1_out[15], subtractor_1_out[16], subtractor_1_out[17], subtractor_1_out[18], subtractor_1_out[19], subtractor_1_out[20], subtractor_1_out[21], subtractor_1_out[22], subtractor_1_out[23], subtractor_1_out[24], subtractor_1_out[25], subtractor_1_out[26], subtractor_1_out[27], subtractor_1_out[28], subtractor_1_out[29], subtractor_1_out[30], subtractor_1_out[31]);
  Adder #(.width(32)) adder_1 (.a(a), .b(b), .out(adder_1_out), .cout(adder_1_cout));  // open: cin
  Subtractor #(.width(32)) subtractor_1 (.a(a), .b(b), .out(subtractor_1_out), .bout(subtractor_1_bout));  // open: bin
  assign and_1_out = a & b;  // AND_Gate and_1, 32 bits wide
  assign or_1_out = a | b;  // OR_Gate or_1, 32 bits wide
  nor nor_2 (nor_2_out, adder_1_out[0], adder_1_out[1], adder_1_out[2], adder_1_out[3], adder_1_out[4], adder_1_out[5], adder_1_out[6], adder_1_out[7], adder_1_out[8], adder_1_out[9], adder_1_out[10], adder_1_out[11], adder_1_out[12], adder_1_out[13], adder_1_out[14], adder_1_out[15], adder_1_out[16], adder_1_out[17], adder_1_out[18], adder_1_out[19], adder_1_out[20], adder_1_out[21], adder_1_out[22], adder_1_out[23], adder_1_out[24], adder_1_out[25], adder_1_out[26], adder_1_out[27], adder_1_out[28], adder_1_out[29], adder_1_out[30], adder_1_out[31]);
  Multiplexer #(.select(2), .width(32)) multiplexer_1 (
    .in0(adder_1_out), .in1(subtractor_1_out), .in2(and_1_out), .in3(or_1_out), .out(Z), .sel(S1S0));
  Multiplexer #(.select(2)) multiplexer_2 (
    .in0(adder_1_cout), .in1(subtractor_1_bout), .in2(1'b0), .in3(1'b0), .out(Cr), .sel(S1S0));
  Multiplexer #(.select(2)) multiplexer_3 (
    .in0(nor_2_out), .in1(nor_1_out), .in2(1'b0), .in3(1'b0), .out(Zr), .sel(S1S0));
endmodule

module REGISTER0to7 (
  input  [31:0] RzD,
  input  RST,
  input  CLK,
  input  [4:0] RaA,
  input  [4:0] RbA,
  input  [4:0] RzA,
  input  [4:0] EnableReEn,
  output [31:0] RaD,
  output [31:0] RbD
);

  wire EN0, EN1, EN2, EN3, EN4, EN5, EN6, EN7, EN8, EN9, EN10, EN11, EN12, EN13, EN14, EN15, EN16, EN17,
       EN18, EN19, EN20, EN21, EN22, EN23, EN24, EN25, EN26, EN27, EN28, EN29, EN30, EN31, undriven;
  wire [31:0] Rin0, Rin1, Rin2, Rin3, Rin4, Rin5, Rin6, Rin7, Rin8, Rin9, Rin10, Rin11, Rin12, Rin13, Rin14,
       Rin15, Rin16, Rin17, Rin18, Rin19, Rin20, Rin21, Rin22, Rin23, Rin24, Rin25, Rin26, Rin27, Rin28,
       Rin29, Rin30, Rin31, Rout0, Rout1, Rout2, Rout3, Rout4, Rout5, Rout6, Rout7, Rout8, Rout9, Rout10,
       Rout11, Rout12, Rout13, Rout14, Rout15, Rout16, Rout17, Rout18, Rout19, Rout20, Rout21, Rout22,
       Rout23, Rout24, Rout25, Rout26, Rout27, Rout28, Rout29, Rout30, Rout31;

  Demultiplexer #(.select(5), .width(32)) demultiplexer_1 (
    .out0(Rin0), .out1(Rin1), .out2(Rin2), .out3(Rin3), .out4(Rin4), .out5(Rin5), .out6(Rin6), .out7(Rin7),
    .out8(Rin8), .out9(Rin9), .out10(Rin10), .out11(Rin11), .out12(Rin12), .out13(Rin13), .out14(Rin14),
    .out15(Rin15), .out16(Rin16), .out17(Rin17), .out18(Rin18), .out19(Rin19), .out20(Rin20), .out21(Rin21),
    .out22(Rin22), .out23(Rin23), .out24(Rin24), .out25(Rin25), .out26(Rin26), .out27(Rin27), .out28(Rin28),
    .out29(Rin29), .out30(Rin30), .out31(Rin31), .in(RzD), .sel(RzA));
  // NoConnect on undriven
  Register #(.width(32)) R0 (.D(Rin0), .en(undriven), .clk(CLK), .Q(Rout0), .clr(RST));
  Register #(.width(32)) R1 (.D(Rin1), .en(EN1), .clk(CLK), .Q(Rout1), .clr(RST));
  Register #(.width(32)) R2 (.D(Rin2), .en(EN2), .clk(CLK), .Q(Rout2), .clr(RST));
  Register #(.width(32)) R3 (.D(Rin3), .en(EN3), .clk(CLK), .Q(Rout3), .clr(RST));
  Register #(.width(32)) R4 (.D(Rin4), .en(EN4), .clk(CLK), .Q(Rout4), .clr(RST));
  Register #(.width(32)) R5 (.D(Rin5), .en(EN5), .clk(CLK), .Q(Rout5), .clr(RST));
  Register #(.width(32)) R6 (.D(Rin6), .en(EN6), .clk(CLK), .Q(Rout6), .clr(RST));
  Register #(.width(32)) R7 (.D(Rin7), .en(EN7), .clk(CLK), .Q(Rout7), .clr(RST));
  Register #(.width(32)) R8 (.D(Rin8), .en(EN8), .clk(CLK), .Q(Rout8), .clr(RST));
  Register #(.width(32)) R9 (.D(Rin9), .en(EN9), .clk(CLK), .Q(Rout9), .clr(RST));
  Register #(.width(32)) R10 (.D(Rin10), .en(EN10), .clk(CLK), .Q(Rout10), .clr(RST));
  Register #(.width(32)) R11 (.D(Rin11), .en(EN11), .clk(CLK), .Q(Rout11), .clr(RST));
  Register #(.width(32)) R12 (.D(Rin12), .en(EN12), .clk(CLK), .Q(Rout12), .clr(RST));
  Register #(.width(32)) R13 (.D(Rin13), .en(EN13), .clk(CLK), .Q(Rout13), .clr(RST));
  Register #(.width(32)) R14 (.D(Rin14), .en(EN14), .clk(CLK), .Q(Rout14), .clr(RST));
  Register #(.width(32)) R15 (.D(Rin15), .en(EN15), .clk(CLK), .Q(Rout15), .clr(RST));
  Register #(.width(32)) R16 (.D(Rin16), .en(EN16), .clk(CLK), .Q(Rout16), .clr(RST));
  Register #(.width(32)) R17 (.D(Rin17), .en(EN17), .clk(CLK), .Q(Rout17), .clr(RST));
  Register #(.width(32)) R18 (.D(Rin18), .en(EN18), .clk(CLK), .Q(Rout18), .clr(RST));
  Register #(.width(32)) R19 (.D(Rin19), .en(EN19), .clk(CLK), .Q(Rout19), .clr(RST));
  Register #(.width(32)) R20 (.D(Rin20), .en(EN20), .clk(CLK), .Q(Rout20), .clr(RST));
  Register #(.width(32)) R21 (.D(Rin21), .en(EN21), .clk(CLK), .Q(Rout21), .clr(RST));
  Multiplexer #(.select(5), .width(32)) multiplexer_1 (
    .in0(Rout0), .in1(Rout1), .in2(Rout2), .in3(Rout3), .in4(Rout4), .in5(Rout5), .in6(Rout6), .in7(Rout7),
    .in8(Rout8), .in9(Rout9), .in10(Rout10), .in11(Rout11), .in12(Rout12), .in13(Rout13), .in14(Rout14),
    .in15(Rout15), .in16(Rout16), .in17(Rout17), .in18(Rout18), .in19(Rout19), .in20(Rout20), .in21(Rout21),
    .in22(Rout22), .in23(Rout23), .in24(Rout24), .in25(Rout25), .in26(Rout26), .in27(Rout27), .in28(Rout28),
    .in29(Rout29), .in30(Rout30), .in31(Rout31), .out(RaD), .sel(RaA));
  Register #(.width(32)) R22 (.D(Rin22), .en(EN22), .clk(CLK), .Q(Rout22), .clr(RST));
  Register #(.width(32)) R23 (.D(Rin23), .en(EN23), .clk(CLK), .Q(Rout23), .clr(RST));
  Register #(.width(32)) R24 (.D(Rin24), .en(EN24), .clk(CLK), .Q(Rout24), .clr(RST));
  Register #(.width(32)) R25 (.D(Rin25), .en(EN25), .clk(CLK), .Q(Rout25), .clr(RST));
  Register #(.width(32)) R26 (.D(Rin26), .en(EN26), .clk(CLK), .Q(Rout26), .clr(RST));
  Register #(.width(32)) R27 (.D(Rin27), .en(EN27), .clk(CLK), .Q(Rout27), .clr(RST));
  Register #(.width(32)) R28 (.D(Rin28), .en(EN28), .clk(CLK), .Q(Rout28), .clr(RST));
  Register #(.width(32)) R29 (.D(Rin29), .en(EN29), .clk(CLK), .Q(Rout29), .clr(RST));
  Register #(.width(32)) R30 (.D(Rin30), .en(EN30), .clk(CLK), .Q(Rout30), .clr(RST));
  Register #(.width(32)) R31 (.D(Rin31), .en(EN31), .clk(CLK), .Q(Rout31), .clr(RST));
  Multiplexer #(.select(5), .width(32)) multiplexer_2 (
    .in0(Rout0), .in1(Rout1), .in2(Rout2), .in3(Rout3), .in4(Rout4), .in5(Rout5), .in6(Rout6), .in7(Rout7),
    .in8(Rout8), .in9(Rout9), .in10(Rout10), .in11(Rout11), .in12(Rout12), .in13(Rout13), .in14(Rout14),
    .in15(Rout15), .in16(Rout16), .in17(Rout17), .in18(Rout18), .in19(Rout19), .in20(Rout20), .in21(Rout21),
    .in22(Rout22), .in23(Rout23), .in24(Rout24), .in25(Rout25), .in26(Rout26), .in27(Rout27), .in28(Rout28),
    .in29(Rout29), .in30(Rout30), .in31(Rout31), .out(RbD), .sel(RbA));
  Decoder #(.select(5)) decoder_1 (
    .out0(EN0), .out1(EN1), .out2(EN2), .out3(EN3), .out4(EN4), .out5(EN5), .out6(EN6), .out7(EN7),
    .out8(EN8), .out9(EN9), .out10(EN10), .out11(EN11), .out12(EN12), .out13(EN13), .out14(EN14),
    .out15(EN15), .out16(EN16), .out17(EN17), .out18(EN18), .out19(EN19), .out20(EN20), .out21(EN21),
    .out22(EN22), .out23(EN23), .out24(EN24), .out25(EN25), .out26(EN26), .out27(EN27), .out28(EN28),
    .out29(EN29), .out30(EN30), .out31(EN31), .sel(EnableReEn), .en(1'b1));

  // Other names for the same wires on the sheet: SDZtunel[4:0] = RzA; SMAtunel[4:0] = RaA; SMBtunel[4:0] = RbA

  // Notes on the sheet:
  //   zero
  //   at
  //   v0
  //   v1
  //   a0
  //   a1
  //   a2
  //   a3
  //   t0
  //   t1
  //   t2
  //   t3
  //   t4
  //   t5
  //   t6
  //   t7
  //   s0
  //   s1
  //   s2
  //   s3
  //   s4
  //   s5
  //   zahid alfahmi
  //   2035446
  //   Ma
  //   fp
  //   s6
  //   s7
  //   t8
  //   t9
  //   k0
  //   k1
  //   gp
  //   sp
  //   r1
  //   Mb
endmodule

module Control (
  input  [18:0] controlinput,
  input  CLK,
  input  RST,
  output [7:0] EnSig,
  output [2:0] RaA,
  output [2:0] RbA,
  output [2:0] RzA,
  output [1:0] ALU
);

  Register #(.width(19)) Control (.D(controlinput), .en(1'b1), .clk(CLK), .Q({ALU, RzA, RbA, RaA, EnSig}), .clr(RST));

  // Notes on the sheet:
  //   En
  //   0-7
  //   Ma
  //   Mb
  //   8-10
  //   11-13
  //   Dz
  //   14-16
  //   ALU
  //   17-18
endmodule

module ControlUnit (
  input  [31:0] mips,
  input  [23:0] counter,
  output [60:0] Inst
);

  wire nor_3_out, nor_4_out, nor_5_out, nor_6_out, nor_7_out;
  wire [1:0] Sel, xor_1_out;
  wire [4:0] demultiplexer_1_out0_2, demultiplexer_1_out0_3;
  wire [10:0] demultiplexer_1_out2;
  wire [15:0] adder_1_out, demultiplexer_1_out0;
  wire [17:1] RtypeOUT;
  wire [25:0] demultiplexer_1_out3;
  wire [25:24] demultiplexer_1_out1;
  wire [58:35] JtypeOUT;
  wire [60:0] ItypeOUT;

  Multiplexer #(.select(2), .width(61)) multiplexer_1 (
    .in0(ItypeOUT), .in1({2'b01, JtypeOUT, {35{1'b0}}}), .in2({{43{1'b0}}, RtypeOUT, 1'b1}),
    .in3({61{1'b0}}), .out(Inst), .sel(Sel));
  nor nor_1 (Sel[1], mips[26], mips[27], mips[28], mips[29], mips[30], mips[31]);
  nor nor_2 (Sel[0], mips[26], ~mips[27], mips[28], mips[29], mips[30], mips[31]);  // NOR_Gate
  Demultiplexer #(.select(2), .width(26)) demultiplexer_1 (
    .out0({demultiplexer_1_out0_2, demultiplexer_1_out0_3, demultiplexer_1_out0}),
    .out1({demultiplexer_1_out1, JtypeOUT}),
    .out2({RtypeOUT[5:1], RtypeOUT[10:6], RtypeOUT[15:11], demultiplexer_1_out2}),
    .out3(demultiplexer_1_out3), .in(mips[25:0]), .sel(Sel));
  nor nor_3 (nor_3_out, ~mips[26], mips[27], mips[28], ~mips[29], mips[30], mips[31]);  // NOR_Gate
  xor xor_1 (xor_1_out[0], mips[26], nor_3_out);
  nor nor_4 (nor_4_out, mips[26], mips[27], ~mips[28], mips[29], mips[30], ~mips[31]);  // NOR_Gate
  or or_1 (xor_1_out[1], mips[28], nor_4_out);
  nor nor_5 (nor_5_out, demultiplexer_1_out2[0], ~demultiplexer_1_out2[1], demultiplexer_1_out2[2], demultiplexer_1_out2[3], demultiplexer_1_out2[4], ~demultiplexer_1_out2[5]);  // NOR_Gate
  Adder #(.width(16)) adder_1 (.a(demultiplexer_1_out0), .b(counter[15:0]), .out(adder_1_out));  // open: cin, cout
  or or_2 (RtypeOUT[16], demultiplexer_1_out2[0], nor_5_out);
  nor nor_6 (nor_6_out, demultiplexer_1_out2[0], demultiplexer_1_out2[1], ~demultiplexer_1_out2[2], demultiplexer_1_out2[3], demultiplexer_1_out2[4], ~demultiplexer_1_out2[5]);  // NOR_Gate
  or or_3 (RtypeOUT[17], demultiplexer_1_out2[0], nor_6_out);
  Multiplexer #(.width(61)) multiplexer_2 (
    .in0({27'h1, demultiplexer_1_out0, xor_1_out, {5{1'b0}}, demultiplexer_1_out0_3, demultiplexer_1_out0_2, 1'b1}),
    .in1({10'h200, adder_1_out, 24'h20, demultiplexer_1_out0_3, demultiplexer_1_out0_2, 1'b0}),
    .out(ItypeOUT), .sel(nor_7_out));
  nor nor_7 (nor_7_out, ~mips[26], mips[27], ~mips[28], mips[29], mips[30], mips[31]);  // NOR_Gate
  // also tied to GND on the sheet: {demultiplexer_1_out2[6], demultiplexer_1_out2[7], demultiplexer_1_out2[8], demultiplexer_1_out2[9], demultiplexer_1_out2[10], demultiplexer_1_out3[0], demultiplexer_1_out3[1], demultiplexer_1_out3[2], demultiplexer_1_out3[3], demultiplexer_1_out3[4], demultiplexer_1_out3[5], demultiplexer_1_out3[6], demultiplexer_1_out3[7], demultiplexer_1_out3[8], demultiplexer_1_out3[9], demultiplexer_1_out3[10], demultiplexer_1_out3[11], demultiplexer_1_out3[12], demultiplexer_1_out3[13], demultiplexer_1_out3[14], demultiplexer_1_out3[15], demultiplexer_1_out3[16], demultiplexer_1_out3[17], demultiplexer_1_out3[18], demultiplexer_1_out3[19], demultiplexer_1_out3[20], demultiplexer_1_out3[21], demultiplexer_1_out3[22], demultiplexer_1_out3[23], demultiplexer_1_out3[24], demultiplexer_1_out3[25], counter[16], counter[17], counter[18], counter[19], counter[20], counter[21], counter[22], counter[23]}

  // Other names for the same wires on the sheet: op[5:0] = mips[31:26]

  // Notes on the sheet:
  //   I type
  //   J type
  //   R type
  //   alu
  //   sa
  //   rd
  //   rb
  //   ra
  //   bne
  //   bne
  //   60
  //   Jump
  //   59
  //   addres
  //   35-58
  //   M3Sel
  //   34
  //   value
  //   18-33
  //   ALU
  //   16-17
  //   Dz
  //   11-15
  //   Mb
  //   6-10
  //   Ma
  //   1-5
  //   En
  //   0
endmodule

module if_id (
  input  [23:0] inPC,
  input  clk,
  input  reset,
  input  [31:0] INST,
  input  [4:0] rd,
  input  [4:0] rs,
  input  [4:0] rt,
  output [23:0] OPC,
  output [15:0] IMM16,
  output [25:0] IMM26,
  output [5:0] op,
  output [4:0] rdo,
  output [4:0] rso,
  output [4:0] rto
);

  Register #(.width(24)) register_1 (.D(inPC), .en(1'b1), .clk(clk), .Q(OPC));  // open: clr
  Register #(.width(32)) register_2 (.D(INST), .en(1'b1), .clk(clk), .Q({op, IMM26[25:16], IMM16}), .clr(reset));
  Register #(.width(15)) register_3 (.D({rt, rs, rd}), .en(1'b1), .clk(clk), .Q({rto, rso, rdo}), .clr(reset));

  assign IMM26[15:0] = IMM16;
endmodule

module id_ex (
  input  [25:0] J_add,
  input  [23:0] Pc,
  input  [15:0] imm16,
  input  [31:0] A_input,
  input  [5:0] func,
  input  clk,
  input  reset,
  input  [31:0] B_input,
  input  [4:0] Rd2in,
  output [25:0] J_addrs,
  output [23:0] Npc,
  output [15:0] im16,
  output [31:0] A_out,
  output [5:0] fun,
  output [31:0] B_out,
  output [4:0] Rd2
);

  Register #(.width(26)) register_1 (.D(J_add), .en(1'b1), .clk(clk), .Q(J_addrs), .clr(reset));
  Register #(.width(5)) register_2 (.D(Rd2in), .en(1'b1), .clk(clk), .Q(Rd2), .clr(reset));
  Register #(.width(32)) A (.D(A_input), .en(1'b1), .clk(clk), .Q(A_out), .clr(reset));
  Register #(.width(32)) B (.D(B_input), .en(1'b1), .clk(clk), .Q(B_out), .clr(reset));
  Register #(.width(24)) register_3 (.D(Pc), .en(1'b1), .clk(clk), .Q(Npc), .clr(reset));
  Register #(.width(6)) register_4 (.D(func), .en(1'b1), .clk(clk), .Q(fun), .clr(reset));
  Register #(.width(16)) register_5 (.D(imm16), .en(1'b1), .clk(clk), .Q(im16), .clr(reset));
endmodule

module ex_mem (
  input  [31:0] alu_input,
  input  clk,
  input  reset,
  input  [4:0] Rd3in,
  output [31:0] alu_out,
  output [4:0] Rd3
);

  Register #(.width(32)) alu (.D(alu_input), .en(1'b1), .clk(clk), .Q(alu_out), .clr(reset));
  Register #(.width(5)) register_1 (.D(Rd3in), .en(1'b1), .clk(clk), .Q(Rd3), .clr(reset));
endmodule

module mem_wb (
  input  [31:0] mem_in,
  input  clk,
  input  reset,
  input  [4:0] Rd4in,
  output [31:0] mem_out,
  output [4:0] Rd4
);

  Register #(.width(32)) mem (.D(mem_in), .en(1'b1), .clk(clk), .Q(mem_out), .clr(reset));
  Register #(.width(5)) register_1 (.D(Rd4in), .en(1'b1), .clk(clk), .Q(Rd4), .clr(reset));
endmodule

module pctoif (
  input  [23:0] pc_iput,
  input  enable,
  input  clk,
  input  reset,
  output [23:0] out_5
);

  Register #(.width(24)) register_1 (.D(pc_iput), .en(enable), .clk(clk), .Q(out_5), .clr(reset));
endmodule

module controlSigs (
  input  [60:0] translated_in,
  output bne,
  output [23:0] addres,
  output [15:0] value,
  output [4:0] dz,
  output [4:0] ma,
  output jump,
  output m3sel,
  output [1:0] alu,
  output [4:0] mb,
  output en
);


  assign addres = translated_in[58:35];
  assign alu = translated_in[17:16];
  assign bne = translated_in[60];
  assign dz = translated_in[15:11];
  assign en = translated_in[0];
  assign jump = translated_in[59];
  assign m3sel = translated_in[34];
  assign ma = translated_in[5:1];
  assign mb = translated_in[10:6];
  assign value = translated_in[33:18];

  // Notes on the sheet:
  //   bne
  //   60
  //   Jump
  //   59
  //   addres
  //   35-58
  //   M3Sel
  //   34
  //   value
  //   18-33
  //   ALU
  //   16-17
  //   Dz
  //   11-15
  //   Mb
  //   6-10
  //   Ma
  //   1-5
  //   En
  //   0
endmodule

module next_pc (
  input  [23:0] INCpc,
  input  J,
  input  [25:0] ADDRES_J,
  input  bNE,
  input  [31:0] Ainput,
  input  [31:0] Binput,
  output PCSrc,
  output [23:0] J_OR_BR_ADDRES
);

  wire and_1_out, comparator_1_eq;
  wire [15:0] adder_1_out;
  wire [31:24] multiplexer_1_out;

  // NoConnect on ADDRES_J[25:16]
  Comparator #(.width(32)) comparator_1 (.a(Ainput), .b(Binput), .eq(comparator_1_eq));  // open: gt, lt
  Adder #(.width(16)) adder_1 (.a(INCpc[15:0]), .b(ADDRES_J[15:0]), .out(adder_1_out));  // open: cin, cout
  Multiplexer #(.width(32)) multiplexer_1 (
    .in0({{16{1'b0}}, adder_1_out}), .in1({{6{1'b0}}, ADDRES_J}), .out({multiplexer_1_out, J_OR_BR_ADDRES}),
    .sel(J));
  or or_1 (PCSrc, and_1_out, J);
  and and_1 (and_1_out, ~comparator_1_eq, bNE);  // AND_Gate
endmodule

module Hazard (
  input  [4:0] Rt,
  input  [4:0] Rs,
  input  EX_Regwrite,
  input  [4:0] Rd2,
  input  MEM_Regwrite,
  input  [4:0] Rd3,
  input  WB_Regwrite,
  input  [4:0] Rd4,
  output [1:0] ForwardA,
  output [1:0] ForwardB
);

  wire and_1_out, and_2_out, and_3_out, and_4_out, and_5_out, and_6_out, comparator_1_eq, comparator_2_eq,
       comparator_3_eq, comparator_4_eq, comparator_5_eq, comparator_6_eq, comparator_7_eq, comparator_8_eq,
       comparator_9_eq, comparator_10_eq, comparator_11_eq, comparator_12_eq, not_1_out, not_2_out,
       not_3_out, not_4_out, not_5_out, not_6_out, not_7_out, not_8_out, not_9_out, not_10_out;

  Comparator #(.width(5)) comparator_1 (.a(Rs), .b({5{1'b0}}), .eq(comparator_1_eq));  // open: gt, lt
  not not_1 (not_1_out, comparator_2_eq);
  Comparator #(.width(5)) comparator_2 (.a(Rs), .b({5{1'b0}}), .eq(comparator_2_eq));  // open: gt, lt
  not not_2 (not_2_out, comparator_3_eq);
  Comparator #(.width(5)) comparator_3 (.a(Rs), .b({5{1'b0}}), .eq(comparator_3_eq));  // open: gt, lt
  not not_3 (not_3_out, comparator_4_eq);
  Comparator #(.width(5)) comparator_4 (.a(Rt), .b({5{1'b0}}), .eq(comparator_4_eq));  // open: gt, lt
  Comparator #(.width(5)) comparator_5 (.a(Rt), .b({5{1'b0}}), .eq(comparator_5_eq));  // open: gt, lt
  not not_4 (not_4_out, comparator_6_eq);
  Comparator #(.width(5)) comparator_6 (.a(Rt), .b({5{1'b0}}), .eq(comparator_6_eq));  // open: gt, lt
  not not_5 (not_5_out, comparator_1_eq);
  not not_6 (not_6_out, comparator_5_eq);
  Comparator #(.width(5)) comparator_7 (.a(Rs), .b(Rd3), .eq(comparator_7_eq));  // open: gt, lt
  Comparator #(.width(5)) comparator_8 (.a(Rs), .b(Rd4), .eq(comparator_8_eq));  // open: gt, lt
  Comparator #(.width(5)) comparator_9 (.a(Rt), .b(Rd2), .eq(comparator_9_eq));  // open: gt, lt
  Comparator #(.width(5)) comparator_10 (.a(Rt), .b(Rd4), .eq(comparator_10_eq));  // open: gt, lt
  Comparator #(.width(5)) comparator_11 (.a(Rs), .b(Rd2), .eq(comparator_11_eq));  // open: gt, lt
  Comparator #(.width(5)) comparator_12 (.a(Rt), .b(Rd3), .eq(comparator_12_eq));  // open: gt, lt
  and and_1 (and_1_out, not_5_out, comparator_11_eq, EX_Regwrite);
  and and_2 (and_2_out, not_1_out, comparator_7_eq, MEM_Regwrite);
  and and_3 (and_3_out, not_2_out, comparator_8_eq, WB_Regwrite);
  and and_4 (and_4_out, not_3_out, comparator_9_eq, EX_Regwrite);
  and and_5 (and_5_out, not_6_out, comparator_12_eq, MEM_Regwrite);
  and and_6 (and_6_out, not_4_out, comparator_10_eq, WB_Regwrite);
  not not_7 (not_7_out, and_1_out);
  not not_8 (not_8_out, and_4_out);
  not not_9 (not_9_out, and_5_out);
  not not_10 (not_10_out, and_2_out);
  Multiplexer multiplexer_1 (.in0(and_5_out), .in1(not_9_out), .out(ForwardB[1]), .sel(and_6_out));
  Multiplexer multiplexer_2 (.in0(and_1_out), .in1(not_7_out), .out(ForwardA[0]), .sel(and_3_out));
  Multiplexer multiplexer_3 (.in0(and_2_out), .in1(not_10_out), .out(ForwardA[1]), .sel(and_3_out));
  Multiplexer multiplexer_4 (.in0(and_4_out), .in1(not_8_out), .out(ForwardB[0]), .sel(and_6_out));
endmodule

module CONTROLNEW (
  input  [5:0] Opcode,
  input  bne,
  output MemRead,
  output MemWrite,
  output RegDst,
  output RegWrite,
  output MemtoReg
);

  wire addi_out, R_TYPE_out;

  and addi (addi_out, ~Opcode[0], ~Opcode[1], ~Opcode[2], Opcode[3], ~Opcode[4], ~Opcode[5]);  // AND_Gate
  and R_TYPE (R_TYPE_out, ~Opcode[0], ~Opcode[1], ~Opcode[2], ~Opcode[2], ~Opcode[3], ~Opcode[4]);  // AND_Gate
  and sw (MemWrite, Opcode[0], ~Opcode[1], Opcode[2], ~Opcode[3], Opcode[4], Opcode[5]);  // AND_Gate
  and lw (MemRead, Opcode[0], Opcode[1], Opcode[2], ~Opcode[3], Opcode[4], ~Opcode[5]);  // AND_Gate
  or or_1 (RegWrite, R_TYPE_out, addi_out, MemRead);
  or or_2 (RegDst, R_TYPE_out, bne);

  assign MemtoReg = MemRead;
endmodule

module ALU_CONTROL (
  input  ALUop,
  input  [5:0] Func,
  output [1:0] ALUCtrl
);

  wire and_1_out, or_1_out, xor_1_out;

  and and_1 (and_1_out, ~Func[4], Func[5]);  // AND_Gate
  xor xor_1 (xor_1_out, ALUop, Func[0]);
  or or_1 (or_1_out, ALUop, Func[1]);
  or or_2 (ALUCtrl[0], xor_1_out, or_1_out);
  or or_3 (ALUCtrl[1], Func[3], and_1_out);
endmodule

module EX (
  input  J,
  input  BNE,
  input  BEQ,
  input  CLK,
  input  MemRead,
  input  RST,
  input  MemWrite,
  input  RegWrite,
  input  MemtoReg,
  input  ALUSrc,
  input  ALUop,
  output Jout,
  output BNEout,
  output BEQout,
  output MemReadO,
  output MemWriteO,
  output RegwriteO,
  output MemReg,
  output AluSrcO,
  output ALuopO
);

  Register #(.width(9)) register_1 (
    .D({ALUop, ALUSrc, MemtoReg, RegWrite, MemWrite, MemRead, BEQ, BNE, J}), .en(1'b1), .clk(CLK),
    .Q({ALuopO, AluSrcO, MemReg, RegwriteO, MemWriteO, MemReadO, BEQout, BNEout, Jout}), .clr(RST));
endmodule

module MEM (
  input  MemRead,
  input  MemWrite,
  input  RegWrite,
  input  CLK,
  input  RST,
  input  MemtoReg,
  output MemReadO,
  output MemWriteO,
  output RegwriteO,
  output MemReg
);

  Register #(.width(4)) register_1 (
    .D({MemtoReg, RegWrite, MemWrite, MemRead}), .en(1'b1), .clk(CLK),
    .Q({MemReg, RegwriteO, MemWriteO, MemReadO}), .clr(RST));
endmodule

module WB (
  input  reg_write_in,
  input  clk,
  input  rest,
  output reg_write
);

  Register #(.width(1)) register_1 (.D(reg_write_in), .en(1'b1), .clk(clk), .Q(reg_write), .clr(rest));
endmodule
