// Logisim project mode.circ as structural Verilog: 5 circuits, main circuit main
module main (
  input  switch,
  input  [31:0] divideS,
  input  rst,
  input  ens,
  input  enb
);

  wire ALU_1_cr, ALU_1_zr, and_1_out, bneTunel, CLK, counter_1_carry, Enabletunel, JumpTunel,
       LoadCounterInput, M3S;
  wire [1:0] SALUtunel;
  wire [4:0] RaAtunnel, RbAtunel, RzAtunel;
  wire [7:0] fileRegister_a3;
  wire [15:0] value;
  wire [23:0] fileRegister_a3_2, LoadAddresTunel, pc;
  wire [31:0] fileRegister_a2, fileRegister_ra, fileRegister_rad, fileRegister_rbd, mipsreg_q,
       multiplexer_1_out, opD, RzDtunel;
  wire [60:0] ControlConvert_inst;

  Register #(.width(32)) mipsreg (.D(opD), .en(1'b1), .clk(CLK), .Q(mipsreg_q), .clr(rst));
  Clock clock_1 (.out(CLK));
  ControlUnit ControlConvert (.mips(mipsreg_q), .counter(pc), .Inst(ControlConvert_inst));
  // NoConnect on fileRegister_a3[7]
  // NoConnect on fileRegister_a3_2
  _7_Segment_Display first (
    .g(fileRegister_a3[6]), .f(fileRegister_a3[5]), .a(fileRegister_a3[0]), .b(fileRegister_a3[1]),
    .e(fileRegister_a3[4]), .d(fileRegister_a3[3]), .c(fileRegister_a3[2]), .dp(fileRegister_a3[2]));
  REGISTER0to7 fileRegister (
    .RzD(RzDtunel), .switch(switch), .RST(rst), .CLK(CLK), .RaA(RaAtunnel), .RbA(RbAtunel), .RzA(RzAtunel),
    .EnableReEn(Enabletunel), .divideon(divideS), .ens(ens), .divideB(divideS), .enb(enb),
    .RaD(fileRegister_rad), .RbD(fileRegister_rbd), .a2(fileRegister_a2),
    .a3({fileRegister_a3_2, fileRegister_a3}), .ra(fileRegister_ra));
  Register #(.width(61)) Control (
    .D(ControlConvert_inst), .en(1'b1), .clk(CLK),
    .Q({bneTunel, JumpTunel, LoadAddresTunel, M3S, value, SALUtunel, RzAtunel, RbAtunel, RaAtunnel, Enabletunel}),
    .clr(rst));
  // NoConnect on fileRegister_a2[31:8]
  // NoConnect on fileRegister_a2[7]
  Multiplexer #(.width(32)) multiplexer_1 (
    .in0(fileRegister_rbd), .in1({{16{1'b0}}, value}), .out(multiplexer_1_out), .sel(M3S));
  _7_Segment_Display second (
    .g(fileRegister_a2[6]), .f(fileRegister_a2[5]), .a(fileRegister_a2[0]), .b(fileRegister_a2[1]),
    .e(fileRegister_a2[4]), .d(fileRegister_a2[3]), .c(fileRegister_a2[2]), .dp(fileRegister_a2[2]));
  // NoConnect on fileRegister_ra[31:8]
  AlU ALU_1 (.a(fileRegister_rad), .b(multiplexer_1_out), .S1S0(SALUtunel), .Z(RzDtunel), .Cr(ALU_1_cr), .Zr(ALU_1_zr));
  // NoConnect on fileRegister_ra[7]
  _7_Segment_Display third (
    .g(fileRegister_ra[6]), .f(fileRegister_ra[5]), .a(fileRegister_ra[0]), .b(fileRegister_ra[1]),
    .e(fileRegister_ra[4]), .d(fileRegister_ra[3]), .c(fileRegister_ra[2]), .dp(fileRegister_ra[2]));
  // NoConnect on ALU_1_cr
  and and_1 (and_1_out, ~ALU_1_zr, bneTunel);  // AND_Gate
  Multiplexer multiplexer_2 (.in0(JumpTunel), .in1(and_1_out), .out(LoadCounterInput), .sel(bneTunel));
  // NoConnect on RzDtunel
  Counter #(.max('hffffff), .width(24)) counter_1 (
    .clr(rst), .load(LoadCounterInput), .up(1'b1), .count(1'b1), .clk(CLK), .D(LoadAddresTunel),
    .carry(counter_1_carry), .Q(pc));
  // NoConnect on counter_1_carry
  ROM #(.addrWidth(24), .dataWidth(32)) RegisterMemory (.addr(pc), .data(opD));

  // Notes on the sheet:
  //   this program  show reminder and qutaion
  //   reminder and denuminator
  //   bne
  //   60
  //   q2/numinator
  //   Jump
  //   59
  //   addres
  //   35-58
  //   q1/numinator
  //   M3Sel
  //   34
  //   value
  //   18-33
  //   ALU
  //   16-17
  //   Dz
  //   11-15
  //   Mb
  //   6-10
  //   Ma
  //   1-5
  //   En
  //   0
  //   contents of RegisterMemory (hex, n*v repeats v):
  //   240b0000 17e5825 240c0000 19d6025 240d0000 2412000a 32730000 32940000 24050080 241a0001 1725822
  //   22730001 31640080 1485fffc 0 0 172a020 27a9822 28a5025 32b50000 32d60000 24050080 241a0001 2729822
  //   22b50001 32640080 1485fffc 0 0 272b020 2baa822 2c94825 32f70000 337b0000 24050080 241a0001 1926022
  //   22f70001 31840080 1485fffc 0 0 192d820 2fab822 3684025 0 0 800017d 4*0 1443fffd 0 0 24010000
  //   24020000 24030000 24040000 24050000 24060000 24070000 24080000 24090000 240a0000 240b0000 240c0000
  //   240d0000 240e0000 240f0000 24100000 24110000 24120000 24130000 24140000 24150000 24160000 24170000
  //   24180000 24190000 241a0000 241b0000 241c0000 241f0000 240b0000 17e5825 240c0000 19d6025 240d0000
  //   32310000 31ad0000 24050080 241a0001 16c5822 22310001 31640080 1485fffc 0 0 16c6820 23a8822 2412000a
  //   32730000 32940000 24050080 241a0001 2328822 22730001 32240080 1485fffc 0 0 232a020 27a9822 28a5025
  //   32b50000 32d60000 24050080 241a0001 2729822 22b50001 32640080 1485fffc 0 0 272b020 2baa822 2c94825
  //   32f70000 337b0000 24050080 241a0001 1b26822 22f70001 31a40080 1485fffc 0 0 1b2d820 2fab822 3684025
  //   240b0000 150b0006 0 0 34e7003f 80000dd 0 0 240b0001 150b0006 0 0 34e70006 80000dd 0 0 240b0002
  //   150b0006 0 0 34e7005b 80000dd 0 0 240b0003 150b0006 0 0 34e7004f 80000dd 0 0 240b0004 150b0006 0 0
  //   34e70066 80000dd 0 0 240b0005 150b0006 0 0 34e7006d 80000dd 0 0 240b0006 150b0006 0 0 34e7007d
  //   80000dd 0 0 240b0007 150b0006 0 0 34e70007 80000dd 0 0 240b0008 150b0006 0 0 34e7007f 80000dd 0 0
  //   240b0009 150bffb6 0 0 34e70067 80000dd 0 0 240b0000 152b0006 0 0 34c6003f 800012d 0 0 240b0001
  //   152b0006 0 0 34c60006 800012d 0 0 240b0002 152b0006 0 0 34c6005b 800012d 0 0 240b0003 152b0006 0 0
  //   34c6004f 800012d 0 0 240b0004 152b0006 0 0 34c60066 800012d 0 0 240b0005 152b0006 0 0 34c6006d
  //   800012d 0 0 240b0006 152b0006 0 0 34c6007d 800012d 0 0 240b0007 152b0006 0 0 34c60007 800012d 0 0
  //   240b0008 152b0006 0 0 34c6007f 800012d 0 0 240b0009 152bffb6 0 0 34c60067 800012d 0 0 240b0000
  //   154b0006 0 0 37ff003f 800026b 0 0 240b0001 154b0006 0 0 37ff0006 800026b 0 0 240b0002 154b0006 0 0
  //   37ff005b 800026b 0 0 240b0003 154b0006 0 0 37ff004f 800026b 0 0 240b0004 154b0006 0 0 37ff0066
  //   800026b 0 0 240b0005 154b0006 0 0 37ff006d 800026b 0 0 240b0006 154b0006 0 0 37ff007d 800026b 0 0
  //   240b0007 154b0006 0 0 37ff0007 800026b 0 0 240b0008 154b0006 0 0 37ff007f 800026b 0 0 240b0009
  //   154bffb6 0 0 37ff0067 800026b 0 0 240b0000 150b0006 0 0 34e7003f 80001cd 0 0 240b0001 150b0006 0 0
  //   34e70006 80001cd 0 0 240b0002 150b0006 0 0 34e7005b 80001cd 0 0 240b0003 150b0006 0 0 34e7004f
  //   80001cd 0 0 240b0004 150b0006 0 0 34e70066 80001cd 0 0 240b0005 150b0006 0 0 34e7006d 80001cd 0 0
  //   240b0006 150b0006 0 0 34e7007d 80001cd 0 0 240b0007 150b0006 0 0 34e70007 80001cd 0 0 240b0008
  //   150b0006 0 0 34e7007f 80001cd 0 0 240b0009 150bffb6 0 0 34e70067 80001cd 0 0 240b0000 152b0006 0 0
  //   34c6003f 800021d 0 0 240b0001 152b0006 0 0 34c60006 800021d 0 0 240b0002 152b0006 0 0 34c6005b
  //   800021d 0 0 240b0003 152b0006 0 0 34c6004f 800021d 0 0 240b0004 152b0006 0 0 34c60066 800021d 0 0
  //   240b0005 152b0006 0 0 34c6006d 800021d 0 0 240b0006 152b0006 0 0 34c6007d 800021d 0 0 240b0007
  //   152b0006 0 0 34c60007 800021d 0 0 240b0008 152b0006 0 0 34c6007f 800021d 0 0 240b0009 152bffb6 0 0
  //   34c60067 800021d 0 0 240b0000 154b0006 0 0 37ff003f 8000032 0 0 240b0001 154b0006 0 0 37ff0006
  //   8000032 0 0 240b0002 154b0006 0 0 37ff005b 8000032 0 0 240b0003 154b0006 0 0 37ff004f 8000032 0 0
  //   240b0004 154b0006 0 0 37ff0066 8000032 0 0 240b0005 154b0006 0 0 37ff006d 8000032 0 0 240b0006
  //   154b0006 0 0 37ff007d 8000032 0 0 240b0007 154b0006 0 0 37ff0007 8000032 0 0 240b0008 154b0006 0 0
  //   37ff007f 8000032 0 0 240b0009 154bffb6 0 0 37ff0067 8000032
endmodule

module AlU (
  input  [31:0] a,
  input  [31:0] b,
  input  [1:0] S1S0,
  output Cr,
  output [31:0] Z,
  output Zr
);

  wire adder_1_cout, nor_1_out, nor_2_out, subtractor_1_bout;
  wire [31:0] adder_1_out, and_1_out, or_1_out, subtractor_1_out;

  nor nor_1 (nor_1_out, subtractor_1_out[0], subtractor_1_out[1], subtractor_1_out[2], subtractor_1_out[3], subtractor_1_out[4], subtractor_1_out[5], subtractor_1_out[6], subtractor_1_out[7], subtractor_1_out[8], subtractor_1_out[9], subtractor_1_out[10], subtractor_1_out[11], subtractor_1_out[12], subtractor_1_out[13], subtractor_1_out[14], subtractor_1_out[15], subtractor_1_out[16], subtractor_1_out[17], subtractor_1_out[18], subtractor_1_out[19], subtractor_1_out[20], subtractor_1_out[21], subtractor_1_out[22], subtractor_1_out[23], subtractor_1_out[24], subtractor_1_out[25], subtractor_1_out[26], subtractor_1_out[27], subtractor_1_out[28], subtractor_1_out[29], subtractor_1_out[30], subtractor_1_out[31]);
  Adder #(.width(32)) adder_1 (.a(a), .b(b), .out(adder_1_out), .cin(1'b0), .cout(adder_1_cout));
  Subtractor #(.width(32)) subtractor_1 (.a(a), .b(b), .out(subtractor_1_out), .bin(1'b0), .bout(subtractor_1_bout));
  assign and_1_out = a & b;  // AND_Gate and_1, 32 bits wide
  assign or_1_out = a | b;  // OR_Gate or_1, 32 bits wide
  nor nor_2 (nor_2_out, adder_1_out[0], adder_1_out[1], adder_1_out[2], adder_1_out[3], adder_1_out[4], adder_1_out[5], adder_1_out[6], adder_1_out[7], adder_1_out[8], adder_1_out[9], adder_1_out[10], adder_1_out[11], adder_1_out[12], adder_1_out[13], adder_1_out[14], adder_1_out[15], adder_1_out[16], adder_1_out[17], adder_1_out[18], adder_1_out[19], adder_1_out[20], adder_1_out[21], adder_1_out[22], adder_1_out[23], adder_1_out[24], adder_1_out[25], adder_1_out[26], adder_1_out[27], adder_1_out[28], adder_1_out[29], adder_1_out[30], adder_1_out[31]);
  Multiplexer #(.select(2), .width(32)) multiplexer_1 (
    .in0(adder_1_out), .in1(subtractor_1_out), .in2(and_1_out), .in3(or_1_out), .out(Z), .sel(S1S0));
  Multiplexer #(.select(2)) multiplexer_2 (
    .in0(adder_1_cout), .in1(subtractor_1_bout), .in2(1'b0), .in3(1'b0), .out(Cr), .sel(S1S0));
  Multiplexer #(.select(2)) multiplexer_3 (
    .in0(nor_2_out), .in1(nor_1_out), .in2(1'b0), .in3(1'b0), .out(Zr), .sel(S1S0));
endmodule

module REGISTER0to7 (
  input  [31:0] RzD,
  input  switch,
  input  RST,
  input  CLK,
  input  [4:0] RaA,
  input  [4:0] RbA,
  input  [4:0] RzA,
  input  EnableReEn,
  input  [31:0] divideon,
  input  ens,
  input  [31:0] divideB,
  input  enb,
  output [31:0] RaD,
  output [31:0] RbD,
  output [31:0] a2,
  output [31:0] a3,
  output [31:0] ra
);

  wire decoder_1_out29, decoder_1_out30, EN0, EN1, EN2, EN3, EN4, EN5, EN6, EN7, EN8, EN9, EN10, EN11, EN12,
       EN13, EN14, EN15, EN16, EN17, EN18, EN19, EN20, EN21, EN22, EN23, EN24, EN25, EN26, EN27, EN28, EN31;
  wire [31:0] Rin0, Rin1, Rin2, Rin3, Rin4, Rin5, Rin6, Rin7, Rin8, Rin9, Rin10, Rin11, Rin12, Rin13, Rin14,
       Rin15, Rin16, Rin17, Rin18, Rin19, Rin20, Rin21, Rin22, Rin23, Rin24, Rin25, Rin26, Rin27, Rin28,
       Rin29, Rin30, Rin31, Rout0, Rout1, Rout2, Rout3, Rout4, Rout5, Rout8, Rout9, Rout10, Rout11, Rout12,
       Rout13, Rout14, Rout15, Rout16, Rout17, Rout18, Rout19, Rout20, Rout21, Rout22, Rout23, Rout24,
       Rout25, Rout26, Rout27, Rout28, Rout29, Rout30;

  Demultiplexer #(.select(5), .width(32)) demultiplexer_1 (
    .out0(Rin0), .out1(Rin1), .out2(Rin2), .out3(Rin3), .out4(Rin4), .out5(Rin5), .out6(Rin6), .out7(Rin7),
    .out8(Rin8), .out9(Rin9), .out10(Rin10), .out11(Rin11), .out12(Rin12), .out13(Rin13), .out14(Rin14),
    .out15(Rin15), .out16(Rin16), .out17(Rin17), .out18(Rin18), .out19(Rin19), .out20(Rin20), .out21(Rin21),
    .out22(Rin22), .out23(Rin23), .out24(Rin24), .out25(Rin25), .out26(Rin26), .out27(Rin27), .out28(Rin28),
    .out29(Rin29), .out30(Rin30), .out31(Rin31), .in(RzD), .sel(RzA));
  Register #(.width(32)) R0 (.D(Rin0), .en(EN0), .clk(CLK), .Q(Rout0), .clr(RST));
  Register #(.width(32)) R1 (.D(Rin1), .en(EN1), .clk(CLK), .Q(Rout1), .clr(RST));
  Register #(.width(32)) R2 (.D({switch, {31{1'b0}}}), .en(1'b1), .clk(CLK), .Q(Rout2), .clr(RST));
  Register #(.width(32)) R3 (.D(Rin3), .en(EN3), .clk(CLK), .Q(Rout3), .clr(RST));
  Register #(.width(32)) R4 (.D(Rin4), .en(EN4), .clk(CLK), .Q(Rout4), .clr(RST));
  Register #(.width(32)) R5 (.D(Rin5), .en(EN5), .clk(CLK), .Q(Rout5), .clr(RST));
  Register #(.width(32)) R6 (.D(Rin6), .en(EN6), .clk(CLK), .Q(a2), .clr(RST));
  Register #(.width(32)) R7 (.D(Rin7), .en(EN7), .clk(CLK), .Q(a3), .clr(RST));
  Register #(.width(32)) R8 (.D(Rin8), .en(EN8), .clk(CLK), .Q(Rout8), .clr(RST));
  Register #(.width(32)) R9 (.D(Rin9), .en(EN9), .clk(CLK), .Q(Rout9), .clr(RST));
  Register #(.width(32)) R10 (.D(Rin10), .en(EN10), .clk(CLK), .Q(Rout10), .clr(RST));
  Register #(.width(32)) R11 (.D(Rin11), .en(EN11), .clk(CLK), .Q(Rout11), .clr(RST));
  Register #(.width(32)) R12 (.D(Rin12), .en(EN12), .clk(CLK), .Q(Rout12), .clr(RST));
  Register #(.width(32)) R13 (.D(Rin13), .en(EN13), .clk(CLK), .Q(Rout13), .clr(RST));
  Register #(.width(32)) R14 (.D(Rin14), .en(EN14), .clk(CLK), .Q(Rout14), .clr(RST));
  Register #(.width(32)) R15 (.D(Rin15), .en(EN15), .clk(CLK), .Q(Rout15), .clr(RST));
  Register #(.width(32)) R16 (.D(Rin16), .en(EN16), .clk(CLK), .Q(Rout16), .clr(RST));
  Register #(.width(32)) R17 (.D(Rin17), .en(EN17), .clk(CLK), .Q(Rout17), .clr(RST));
  Register #(.width(32)) R18 (.D(Rin18), .en(EN18), .clk(CLK), .Q(Rout18), .clr(RST));
  Register #(.width(32)) R19 (.D(Rin19), .en(EN19), .clk(CLK), .Q(Rout19), .clr(RST));
  Register #(.width(32)) R20 (.D(Rin20), .en(EN20), .clk(CLK), .Q(Rout20), .clr(RST));
  Register #(.width(32)) R21 (.D(Rin21), .en(EN21), .clk(CLK), .Q(Rout21), .clr(RST));
  Multiplexer #(.select(5), .width(32)) multiplexer_1 (
    .in0(Rout0), .in1(Rout1), .in2(Rout2), .in3(Rout3), .in4(Rout4), .in5(Rout5), .in6(a2), .in7(a3),
    .in8(Rout8), .in9(Rout9), .in10(Rout10), .in11(Rout11), .in12(Rout12), .in13(Rout13), .in14(Rout14),
    .in15(Rout15), .in16(Rout16), .in17(Rout17), .in18(Rout18), .in19(Rout19), .in20(Rout20), .in21(Rout21),
    .in22(Rout22), .in23(Rout23), .in24(Rout24), .in25(Rout25), .in26(Rout26), .in27(Rout27), .in28(Rout28),
    .in29(Rout29), .in30(Rout30), .in31(ra), .out(RaD), .sel(RaA));
  Register #(.width(32)) R22 (.D(Rin22), .en(EN22), .clk(CLK), .Q(Rout22), .clr(RST));
  Register #(.width(32)) R23 (.D(Rin23), .en(EN23), .clk(CLK), .Q(Rout23), .clr(RST));
  Register #(.width(32)) R24 (.D(Rin24), .en(EN24), .clk(CLK), .Q(Rout24), .clr(RST));
  Register #(.width(32)) R25 (.D(Rin25), .en(EN25), .clk(CLK), .Q(Rout25), .clr(RST));
  Register #(.width(32)) R26 (.D(Rin26), .en(EN26), .clk(CLK), .Q(Rout26), .clr(RST));
  Register #(.width(32)) R27 (.D(Rin27), .en(EN27), .clk(CLK), .Q(Rout27), .clr(RST));
  Register #(.width(32)) R28 (.D(Rin28), .en(EN28), .clk(CLK), .Q(Rout28), .clr(RST));
  Register #(.width(32)) R29 (.D(divideon), .en(ens), .clk(CLK), .Q(Rout29), .clr(1'b0));
  Register #(.width(32)) R30 (.D(divideB), .en(enb), .clk(CLK), .Q(Rout30), .clr(1'b0));
  Register #(.width(32)) R31 (.D(Rin31), .en(EN31), .clk(CLK), .Q(ra), .clr(RST));
  Multiplexer #(.select(5), .width(32)) multiplexer_2 (
    .in0(Rout0), .in1(Rout1), .in2(Rout2), .in3(Rout3), .in4(Rout4), .in5(Rout5), .in6(a2), .in7(a3),
    .in8(Rout8), .in9(Rout9), .in10(Rout10), .in11(Rout11), .in12(Rout12), .in13(Rout13), .in14(Rout14),
    .in15(Rout15), .in16(Rout16), .in17(Rout17), .in18(Rout18), .in19(Rout19), .in20(Rout20), .in21(Rout21),
    .in22(Rout22), .in23(Rout23), .in24(Rout24), .in25(Rout25), .in26(Rout26), .in27(Rout27), .in28(Rout28),
    .in29(Rout29), .in30(Rout30), .in31(ra), .out(RbD), .sel(RbA));
  Decoder #(.select(5)) decoder_1 (
    .out0(EN0), .out1(EN1), .out2(EN2), .out3(EN3), .out4(EN4), .out5(EN5), .out6(EN6), .out7(EN7),
    .out8(EN8), .out9(EN9), .out10(EN10), .out11(EN11), .out12(EN12), .out13(EN13), .out14(EN14),
    .out15(EN15), .out16(EN16), .out17(EN17), .out18(EN18), .out19(EN19), .out20(EN20), .out21(EN21),
    .out22(EN22), .out23(EN23), .out24(EN24), .out25(EN25), .out26(EN26), .out27(EN27), .out28(EN28),
    .out29(decoder_1_out29), .out30(decoder_1_out30), .out31(EN31), .sel(RzA), .en(EnableReEn));
  // NoConnect on decoder_1_out29
  // NoConnect on decoder_1_out30

  // Other names for the same wires on the sheet: Rout6[31:0] = a2; Rout7[31:0] = a3; Rout31[31:0] = ra;
  //   SDZtunel[4:0] = RzA; SMAtunel[4:0] = RaA; SMBtunel[4:0] = RbA

  // Notes on the sheet:
  //   zero
  //   at
  //   v0
  //   v1
  //   a0
  //   a1
  //   a2
  //   a3
  //   t0
  //   t1
  //   t2
  //   t3
  //   t4
  //   t5
  //   t6
  //   t7
  //   s0
  //   s1
  //   s2
  //   s3
  //   s4
  //   s5
  //   Ma
  //   fp
  //   s6
  //   s7
  //   t8
  //   t9
  //   k0
  //   k1
  //   gp
  //   sp
  //   ra
  //   Mb
endmodule

module Control (
  input  [18:0] controlinput,
  input  CLK,
  input  RST,
  output [7:0] EnSig,
  output [2:0] RaA,
  output [2:0] RbA,
  output [2:0] RzA,
  output [1:0] ALU
);

  Register #(.width(19)) Control (.D(controlinput), .en(1'b1), .clk(CLK), .Q({ALU, RzA, RbA, RaA, EnSig}), .clr(RST));

  // Notes on the sheet:
  //   En
  //   0-7
  //   Ma
  //   Mb
  //   8-10
  //   11-13
  //   Dz
  //   14-16
  //   ALU
  //   17-18
endmodule

module ControlUnit (
  input  [31:0] mips,
  input  [23:0] counter,
  output [60:0] Inst
);

  wire adder_1_cout, nor_3_out, nor_4_out, nor_5_out, nor_6_out, nor_7_out;
  wire [1:0] Sel, xor_1_out;
  wire [4:0] demultiplexer_1_out0_2, demultiplexer_1_out0_3;
  wire [10:0] demultiplexer_1_out2;
  wire [15:0] adder_1_out, demultiplexer_1_out0;
  wire [17:1] RtypeOUT;
  wire [25:0] demultiplexer_1_out3;
  wire [25:24] demultiplexer_1_out1;
  wire [58:35] JtypeOUT;
  wire [60:0] ItypeOUT;

  Multiplexer #(.select(2), .width(61)) multiplexer_1 (
    .in0(ItypeOUT), .in1({2'b01, JtypeOUT, {35{1'b0}}}), .in2({{43{1'b0}}, RtypeOUT, 1'b1}),
    .in3({61{1'b0}}), .out(Inst), .sel(Sel));
  nor nor_1 (Sel[1], mips[26], mips[27], mips[28], mips[29], mips[30], mips[31]);
  nor nor_2 (Sel[0], mips[26], ~mips[27], mips[28], mips[29], mips[30], mips[31]);  // NOR_Gate
  Demultiplexer #(.select(2), .width(26)) demultiplexer_1 (
    .out0({demultiplexer_1_out0_2, demultiplexer_1_out0_3, demultiplexer_1_out0}),
    .out1({demultiplexer_1_out1, JtypeOUT}),
    .out2({RtypeOUT[5:1], RtypeOUT[10:6], RtypeOUT[15:11], demultiplexer_1_out2}),
    .out3(demultiplexer_1_out3), .in(mips[25:0]), .sel(Sel));
  // NoConnect on demultiplexer_1_out3
  nor nor_3 (nor_3_out, ~mips[26], mips[27], mips[28], ~mips[29], mips[30], mips[31]);  // NOR_Gate
  xor xor_1 (xor_1_out[0], mips[26], nor_3_out);
  nor nor_4 (nor_4_out, mips[26], mips[27], ~mips[28], mips[29], mips[30], ~mips[31]);  // NOR_Gate
  or or_1 (xor_1_out[1], mips[28], nor_4_out);
  // NoConnect on demultiplexer_1_out2[10:6]
  nor nor_5 (nor_5_out, demultiplexer_1_out2[0], ~demultiplexer_1_out2[1], demultiplexer_1_out2[2], demultiplexer_1_out2[3], demultiplexer_1_out2[4], ~demultiplexer_1_out2[5]);  // NOR_Gate
  // NoConnect on counter[23:16]
  Adder #(.width(16)) adder_1 (
    .a(demultiplexer_1_out0), .b(counter[15:0]), .out(adder_1_out), .cin(1'b0), .cout(adder_1_cout));
  // NoConnect on adder_1_cout
  or or_2 (RtypeOUT[16], demultiplexer_1_out2[0], nor_5_out);
  nor nor_6 (nor_6_out, demultiplexer_1_out2[0], demultiplexer_1_out2[1], ~demultiplexer_1_out2[2], demultiplexer_1_out2[3], demultiplexer_1_out2[4], ~demultiplexer_1_out2[5]);  // NOR_Gate
  or or_3 (RtypeOUT[17], demultiplexer_1_out2[0], nor_6_out);
  Multiplexer #(.width(61)) multiplexer_2 (
    .in0({27'h1, demultiplexer_1_out0, xor_1_out, demultiplexer_1_out0_3, {5{1'b0}}, demultiplexer_1_out0_2, 1'b1}),
    .in1({10'h200, adder_1_out, 24'h20, demultiplexer_1_out0_3, demultiplexer_1_out0_2, 1'b0}),
    .out(ItypeOUT), .sel(nor_7_out));
  nor nor_7 (nor_7_out, ~mips[26], mips[27], ~mips[28], mips[29], mips[30], mips[31]);  // NOR_Gate

  // Other names for the same wires on the sheet: op[5:0] = mips[31:26]

  // Notes on the sheet:
  //   I type
  //   J type
  //   R type
  //   alu
  //   sa
  //   rd
  //   rb
  //   ra
  //   bne
  //   bne
  //   60
  //   Jump
  //   59
  //   addres
  //   35-58
  //   M3Sel
  //   34
  //   value
  //   18-33
  //   ALU
  //   16-17
  //   Dz
  //   11-15
  //   Mb
  //   6-10
  //   Ma
  //   1-5
  //   En
  //   0
endmodule
